# Fritzing sketch Prototipação - Projeto 1.1 (saved by Fritzing 0.9.3b)
breadboards: 1

parts:
  Componente1 = Arduino Mega 2560 (Rev3)  # not connected
  R10 = Resistor [tolerance=±5% resistance=720 package=THT]
  R11 = Resistor [tolerance=±5% resistance=720 package=THT]
  R12 = Resistor [tolerance=±5% resistance=720 package=THT]
  R13 = Resistor [tolerance=±5% resistance=720 package=THT]
  R14 = Resistor [tolerance=±5% resistance=720 package=THT]
  R15 = Resistor [tolerance=±5% resistance=720 package=THT]
  R16 = Resistor [tolerance=±5% resistance=720 package=THT]
  R17 = Resistor [tolerance=±5% resistance=720 package=THT]
  R18 = Resistor [tolerance=±5% resistance=720 package=THT]
  LED1 = LED - 5mm [color="Red (633nm)" package="5 mm [THT]"]
  LED2 = LED - 5mm [color="Red (633nm)" package="5 mm [THT]"]
  LED3 = LED - 5mm [color="Red (633nm)" package="5 mm [THT]"]
  LED4 = LED - 5mm [color="Yellow (595nm)" package="5 mm [THT]"]
  LED5 = LED - 5mm [color="Yellow (595nm)" package="5 mm [THT]"]
  LED6 = LED - 5mm [color="Yellow (595nm)" package="5 mm [THT]"]
  LED7 = LED - 5mm [color="Green (570nm)" package="5 mm [THT]"]
  LED8 = LED - 5mm [color="Green (570nm)" package="5 mm [THT]"]
  LED9 = LED - 5mm [color="Green (570nm)" package="5 mm [THT]"]

nets:
  N1: R10.Pin_1, LED3.anode
  N2: R11.Pin_1, LED6.anode
  N3: R12.Pin_1, LED2.anode
  N4: R13.Pin_1, LED8.anode
  N5: R14.Pin_1, LED4.anode
  N6: R15.Pin_1, LED7.anode
  N7: R16.Pin_1, LED1.anode
  N8: R17.Pin_1, LED5.anode
  N9: R18.Pin_1, LED9.anode
  N10: LED1.cathode, LED2.cathode, LED3.cathode, LED4.cathode, LED5.cathode, LED6.cathode, LED7.cathode, LED8.cathode, LED9.cathode
